# Fritzing sketch 433 Trans (saved by Fritzing 0.9.10b)
circuit board: 3.93736cm x 2.37283cm
stripboards: 1

parts:
  J1 = female pin header, 3 pins [form="♀ (female)"]
  R1 = Resistor [tolerance=±5% resistance=1M power=0.25 package=THT]
  J2 = female pin header, 2 pins [form="♀ (female)"]
  U1 = mystery part, 14 pins [chip_label=Xiao]

nets (from the breadboard view):
  N1: J1.pin1, J1.pin2, R1.Pin_0, J2.pin1, U1.pin1, U1.pin2, U1.pin13, U1.pin14
  N2: J1.pin3, R1.Pin_1, J2.pin2, U1.pin3, U1.pin6, U1.pin9, U1.pin12
  N3: U1.pin4, U1.pin11
  N4: U1.pin5, U1.pin10
  N5: U1.pin7, U1.pin8

notes:
  alicescfernandes
