# Fritzing sketch 433 receiverfzz (saved by Fritzing 0.9.10b)
circuit board: 2.96225cm x 2.46178cm

parts:
  U1 = mystery part, 14 pins [chip_label=ESP32]
  433 = female pin header, 4 pins [form="♀ (female)"]

nets:
  N1: U1.pin2, 433.pin1
  N2: U1.pin13, 433.pin3
  N3: U1.pin14, 433.pin4

notes:
  alicescfernandes
