# Fritzing sketch receiver (saved by Fritzing 0.9.10b)
circuit board: 6.9cm x 4.7cm

parts:
  Whadda_433_TX = mystery part, 3 pins [chip_label=?]
  CONN1 = USB connector [package=THT]
  U1 = ESP32-38PinWide [part_number=ESP32]

nets:
  N1: Whadda_433_TX.pin1, U1.P34
  N2: Whadda_433_TX.pin2, U1.3.3
  GND: Whadda_433_TX.pin3, CONN1.GND, CONN1.chassis5, CONN1.chassis6, U1.GND
  5V: CONN1.5V, U1.VIN

notes:
  alicescfernandes

custom parts:
  ESP32-38PinWide: Generic 38-Pin ESP32 with wide format (only access to one side of pins on a breadboard) based on Stephen Lilley's HiLetgo ESP-WROOM-32 ESP32 ESP-32S Development Board.
