# Fritzing sketch transmitter (saved by Fritzing 0.9.10b)
circuit board: 4.60601cm x 2.55665cm
stripboards: 2

parts:
  R1_1M = Resistor [tolerance=±5% resistance=1M power=0.25 package=THT]
  Xiao = seeeduino-xiao
  VIN = female pin header, 1 pin [form="♀ (female)"]
  GND = female pin header, 1 pin [form="♀ (female)"]
  433_Sensor = female pin header, 3 pins [form="♀ (female)"]

nets:
  N1: R1_1M.Pin_0, Xiao.D5, VIN.pin1
  N2: R1_1M.Pin_1, Xiao.GND, GND.pin1, 433_Sensor.pin3
  N3: Xiao.D7, 433_Sensor.pin1
  N4: Xiao.5V, 433_Sensor.pin2

notes:
  alicescfernandes
  VCC GND DAT

custom parts:
  seeeduino-xiao: Seeeduino XIAO processor board.
